// Logisim project p2orga1.circ as structural Verilog: 13 circuits, main circuit main
module main (
  input  in_1,
  input  in_2,
  output out_3
);

  nor nor_1 (out_3, in_1, in_2);
endmodule

module p2ej4a (
  input  in_1,
  input  in_2,
  input  in_3,
  output out_4
);

  wire nor_1_out, not_1_out, not_2_out, not_3_out, not_4_out;

  not not_1 (not_1_out, in_1);
  not not_2 (not_2_out, in_2);
  not not_3 (not_3_out, in_3);
  nor nor_1 (nor_1_out, not_1_out, not_2_out);
  nor nor_2 (out_4, not_4_out, not_3_out);
  not not_4 (not_4_out, nor_1_out);
endmodule

module p2ej4b (
  input  in_1,
  input  in_2,
  output out_3
);

  nor nor_1 (out_3, in_1, in_2);
endmodule

module p2ej4c (
  input  A,
  input  B,
  input  C,
  input  D,
  output out_5
);

  wire and_1_out, and_2_out, and_3_out, and_4_out, and_5_out, and_6_out, not_1_out, not_2_out, not_3_out,
       not_4_out, not_5_out, or_1_out, or_2_out, or_3_out, or_4_out, or_5_out;

  not not_1 (not_1_out, A);
  not not_2 (not_2_out, B);
  not not_3 (not_3_out, C);
  not not_4 (not_4_out, D);
  not not_5 (not_5_out, D);
  and and_1 (and_1_out, not_1_out, not_2_out);
  and and_2 (and_2_out, not_3_out, not_4_out);
  or or_1 (or_1_out, A, B);
  or or_2 (or_2_out, C, D);
  and and_3 (and_3_out, A, B);
  and and_4 (and_4_out, B, not_5_out);
  and and_5 (and_5_out, and_1_out, and_2_out);
  and and_6 (and_6_out, or_1_out, or_2_out);
  or or_3 (or_3_out, and_3_out, C);
  or or_4 (or_4_out, and_5_out, and_6_out);
  or or_5 (or_5_out, or_3_out, and_4_out);
  and and_7 (out_5, or_4_out, or_5_out);
endmodule

module p2ej5a (
  input  A,
  input  B,
  input  C,
  output out_4
);

  wire and_1_out, and_2_out, and_3_out, and_4_out, and_5_out, and_6_out, and_7_out, and_8_out, not_1_out,
       not_2_out, not_3_out, not_4_out, or_1_out, or_2_out;

  not not_1 (not_1_out, B);
  not not_2 (not_2_out, C);
  not not_3 (not_3_out, B);
  not not_4 (not_4_out, A);
  and and_1 (and_1_out, A, not_1_out);
  and and_2 (and_2_out, A, not_3_out);
  and and_3 (and_3_out, not_4_out, B);
  and and_4 (and_4_out, A, B);
  and and_5 (and_5_out, and_2_out, C);
  and and_6 (and_6_out, and_3_out, C);
  and and_7 (and_7_out, and_4_out, C);
  and and_8 (and_8_out, and_1_out, not_2_out);
  or or_1 (or_1_out, and_8_out, and_5_out);
  or or_2 (or_2_out, and_6_out, and_7_out);
  or or_3 (out_4, or_1_out, or_2_out);
endmodule

module p2ej5fsimplificado (
  input  A,
  input  B,
  input  C,
  output out_4
);

  wire and_1_out, and_2_out, nor_1_out, or_1_out;

  nor nor_1 (nor_1_out, B, C);
  or or_1 (or_1_out, A, B);
  and and_1 (and_1_out, A, nor_1_out);
  and and_2 (and_2_out, C, or_1_out);
  or or_2 (out_4, and_1_out, and_2_out);
endmodule

module p2ej5bGsimplificado (
  input  D,
  input  E,
  input  F,
  output out_4
);

  wire and_1_out, and_2_out, not_1_out, not_2_out, not_3_out, or_1_out, or_2_out;

  not not_1 (not_1_out, E);
  not not_2 (not_2_out, F);
  not not_3 (not_3_out, D);
  or or_1 (or_1_out, D, not_1_out);
  or or_2 (or_2_out, not_3_out, E);
  and and_1 (and_1_out, or_1_out, not_2_out);
  and and_2 (and_2_out, F, or_2_out);
  or or_3 (out_4, and_1_out, and_2_out);
endmodule

module p2ej6inversor (
  input  A,
  input  B,
  input  C,
  input  control,
  output out_5,
  output out_6,
  output out_7
);

  wire and_1_out, and_2_out, and_3_out, and_4_out, and_5_out, and_6_out, not_1_out, not_2_out, not_3_out,
       not_4_out, not_5_out, not_6_out;

  not not_1 (not_1_out, A);
  not not_2 (not_2_out, control);
  not not_3 (not_3_out, B);
  not not_4 (not_4_out, control);
  not not_5 (not_5_out, C);
  not not_6 (not_6_out, control);
  and and_1 (and_1_out, not_1_out, control);
  and and_2 (and_2_out, A, not_2_out);
  and and_3 (and_3_out, not_3_out, control);
  and and_4 (and_4_out, B, not_4_out);
  and and_5 (and_5_out, not_5_out, control);
  and and_6 (and_6_out, C, not_6_out);
  or or_1 (out_5, and_1_out, and_2_out);
  or or_2 (out_6, and_3_out, and_4_out);
  or or_3 (out_7, and_5_out, and_6_out);
endmodule

module sumadorSimple (
  input  A,
  input  B,
  output sum,
  output carry
);

  wire and_1_out, and_2_out, and_3_out, not_1_out, not_2_out, not_3_out;

  not not_1 (not_1_out, A);
  not not_2 (not_2_out, B);
  and and_1 (and_1_out, not_1_out, B);
  and and_2 (and_2_out, A, not_2_out);
  or or_1 (sum, and_1_out, and_2_out);
  and and_3 (and_3_out, B, A);
  not not_3 (not_3_out, sum);
  and and_4 (carry, not_3_out, and_3_out);
endmodule

module sumadorCompleto (
  input  cin,
  input  A,
  input  B,
  output sum,
  output cout
);

  wire sumadorsimple_1_carry, sumadorsimple_1_sum, sumadorsimple_2_carry;

  sumadorSimple sumadorsimple_1 (.A(A), .B(B), .sum(sumadorsimple_1_sum), .carry(sumadorsimple_1_carry));
  sumadorSimple sumadorsimple_2 (.A(cin), .B(sumadorsimple_1_sum), .sum(sum), .carry(sumadorsimple_2_carry));
  or or_1 (cout, sumadorsimple_2_carry, sumadorsimple_1_carry);
endmodule

module p2ej7a (
  input  S0,
  input  S1,
  input  S2,
  input  S3,
  output R0,
  output R1,
  output R2,
  output R3
);

  wire not_1_out, p2ej6inversor_1_out_5, p2ej6inversor_1_out_6, p2ej6inversor_1_out_7,
       sumadorcompleto_1_cout, sumadorcompleto_2_cout, sumadorcompleto_3_cout;

  not not_1 (not_1_out, S0);
  p2ej6inversor p2ej6inversor_1 (
    .A(S1), .B(S2), .C(S3), .control(1'b1), .out_5(p2ej6inversor_1_out_5), .out_6(p2ej6inversor_1_out_6),
    .out_7(p2ej6inversor_1_out_7));
  sumadorCompleto sumadorcompleto_1 (.cin(1'b0), .A(not_1_out), .B(1'b1), .sum(R0), .cout(sumadorcompleto_1_cout));
  sumadorCompleto sumadorcompleto_2 (
    .cin(sumadorcompleto_1_cout), .A(p2ej6inversor_1_out_5), .B(1'b0), .sum(R1), .cout(sumadorcompleto_2_cout));
  sumadorCompleto sumadorcompleto_3 (
    .cin(sumadorcompleto_2_cout), .A(p2ej6inversor_1_out_6), .B(1'b0), .sum(R2), .cout(sumadorcompleto_3_cout));
  sumadorCompleto sumadorcompleto_4 (
    .cin(sumadorcompleto_3_cout), .A(p2ej6inversor_1_out_7), .B(1'b0), .sum(R3));  // open: cout
endmodule

module registroSimple (
  input  d0,
  input  d1,
  input  d2,
  input  d3,
  input  load,
  output o0,
  output o1,
  output o2,
  output o3
);

  wire and_1_out, clk_out, d_ff_1_qn, d_ff_2_qn, d_ff_3_qn, d_ff_4_qn;

  Clock clk (.out(clk_out));
  and and_1 (and_1_out, load, clk_out);
  D_Flip_Flop d_ff_1 (.D(d0), .clk(and_1_out), .Q(o0), .Qn(d_ff_1_qn));  // open: preset, reset
  D_Flip_Flop d_ff_2 (.D(d1), .clk(and_1_out), .Q(o1), .Qn(d_ff_2_qn));  // open: preset, reset
  D_Flip_Flop d_ff_3 (.D(d2), .clk(and_1_out), .Q(o2), .Qn(d_ff_3_qn), .preset(1'b0));  // open: reset
  D_Flip_Flop d_ff_4 (.D(d3), .clk(and_1_out), .Q(o3), .Qn(d_ff_4_qn));  // open: preset, reset
  // also tied to GND on the sheet: {d_ff_1_qn, d_ff_2_qn, d_ff_3_qn, d_ff_4_qn}
endmodule

module registroBidireccional (
  input  d0,
  input  read,
  input  load,
  output out_4
);

  wire clk_out, d_ff_1_q, multiplexer_1_out;

  Multiplexer multiplexer_1 (.in0(d_ff_1_q), .in1(d0), .out(multiplexer_1_out), .sel(load));
  Clock clk (.out(clk_out));
  D_Flip_Flop d_ff_1 (.D(multiplexer_1_out), .clk(clk_out), .Q(d_ff_1_q));  // open: Qn, preset, reset
  assign out_4 = read ? d_ff_1_q : 1'bz;  // Controlled_Buffer controlled_buffer_1
endmodule
