// Logisim project TallerLogica-Combinatorios.circ as structural Verilog: 9 circuits, main circuit verificador
module sumador_simple (
  input  A,
  input  B,
  output S,
  output Cout
);

  xor xor_1 (S, A, B);
  and and_1 (Cout, A, B);
endmodule

module sumador_completo (
  input  Cin,
  input  A,
  input  B,
  output S,
  output Cout
);

  wire and_1_out, and_2_out, xor_1_out;

  xor xor_1 (xor_1_out, A, B);
  and and_1 (and_1_out, B, A);
  xor xor_2 (S, Cin, xor_1_out);
  and and_2 (and_2_out, Cin, xor_1_out);
  sumador_simple sumador_simple_1 ();  // open: A, B, S, Cout
  or or_1 (Cout, and_2_out, and_1_out);
endmodule

module sumador_4 (
  input  Cin,
  input  [3:0] A,
  input  [3:0] B,
  output [3:0] S,
  output Cout
);

  wire sumador_completo_1_cout, sumador_completo_2_cout, sumador_completo_3_cout;

  sumador_completo sumador_completo_1 (.Cin(Cin), .A(A[0]), .B(B[0]), .S(S[0]), .Cout(sumador_completo_1_cout));
  sumador_completo sumador_completo_2 (
    .Cin(sumador_completo_1_cout), .A(A[1]), .B(B[1]), .S(S[1]), .Cout(sumador_completo_2_cout));
  sumador_completo sumador_completo_3 (
    .Cin(sumador_completo_2_cout), .A(A[2]), .B(B[2]), .S(S[2]), .Cout(sumador_completo_3_cout));
  sumador_completo sumador_completo_4 (.Cin(sumador_completo_3_cout), .A(A[3]), .B(B[3]), .S(S[3]), .Cout(Cout));
  Hex_Digit_Display hex_digit_display_1 (.value(S));  // open: dp
endmodule

module comparador_cero (
  input  [3:0] A,
  output Z
);

  wire or_1_out, or_2_out;

  or or_1 (or_1_out, A[0], A[1]);
  or or_2 (or_2_out, A[2], A[3]);
  nor nor_1 (Z, or_1_out, or_2_out);
endmodule

module sumador_flags (
  input  Cin,
  input  [3:0] A,
  input  [3:0] B,
  output [3:0] S,
  output N,
  output Z,
  output V,
  output C
);

  wire and_1_out, and_2_out, and_3_out, nor_1_out, not_1_out;

  and and_1 (and_1_out, A[3], B[3]);
  nor nor_1 (nor_1_out, A[3], B[3]);
  sumador_4 sumador_4_1 (.Cin(Cin), .A(A), .B(B), .S({N, S[2:0]}), .Cout(C));
  comparador_cero comparador_cero_1 (.A({N, S[2:0]}), .Z(Z));
  not not_1 (not_1_out, N);
  and and_2 (and_2_out, not_1_out, and_1_out);
  and and_3 (and_3_out, N, nor_1_out);
  Hex_Digit_Display hex_digit_display_1 (.value({N, S[2:0]}));  // open: dp
  or or_1 (V, and_2_out, and_3_out);

  assign S[3] = N;
endmodule

module incrementador_4 (
  input  [3:0] A,
  output [3:0] S
);

  sumador_4 sumador_4_1 (.Cin(1'b1), .A(A), .S(S));  // open: B, Cout
  Hex_Digit_Display hex_digit_display_1 (.value(S));  // open: dp
endmodule

module inversor_4 (
  input  [3:0] A,
  input  INV,
  output [3:0] S
);

  wire [3:0] incrementador_4_1_s, not_1_out;

  Hex_Digit_Display hex_digit_display_1 (.value(A));  // open: dp
  not not_1 (not_1_out[0], A[0]);
  not not_2 (not_1_out[1], A[1]);
  not not_3 (not_1_out[2], A[2]);
  not not_4 (not_1_out[3], A[3]);
  incrementador_4 incrementador_4_1 (.A(not_1_out), .S(incrementador_4_1_s));
  Multiplexer #(.width(4)) multiplexer_1 (.in0(A), .in1(incrementador_4_1_s), .out(S), .sel(INV));
  Hex_Digit_Display hex_digit_display_2 (.value(S));  // open: dp
endmodule

module ALU (
  input  [3:0] A,
  input  [3:0] B,
  input  [1:0] OP,
  output N,
  output Z,
  output V,
  output C,
  output [3:0] S
);

  wire and_1_out, and_2_out, and_3_out, and_8_out, and_9_out, comparador_cero_1_z, multiplexer_2_out,
       multiplexer_3_out, nor_1_out, nor_2_out, not_1_out, not_2_out, not_3_out, not_4_out, not_5_out,
       not_6_out, not_7_out, not_8_out, not_9_out, or_5_out, or_6_out, sumador_flags_1_c, sumador_flags_1_v,
       xor_1_out;
  wire [3:0] and_4_out, inversor_4_1_s, multiplexer_1_out, or_1_out, sumador_flags_1_s;

  not not_1 (not_1_out, B[3]);
  Hex_Digit_Display hex_digit_display_1 (.value(A), .dp(A[0]));
  Hex_Digit_Display hex_digit_display_2 (.value(B), .dp(B[0]));
  nor nor_1 (nor_1_out, B[0], B[1]);
  and and_1 (and_1_out, nor_1_out, nor_2_out);
  nor nor_2 (nor_2_out, B[2], not_1_out);
  not not_2 (not_2_out, B[0]);
  and and_2 (and_2_out, not_2_out, not_3_out);
  not not_3 (not_3_out, B[1]);
  not not_4 (not_4_out, B[2]);
  and and_3 (and_3_out, and_2_out, not_4_out);
  and and_4 (and_4_out[0], A[0], B[0]);
  and and_5 (and_4_out[1], A[1], B[1]);
  and and_6 (and_4_out[2], A[2], B[2]);
  and and_7 (and_4_out[3], B[3], A[3]);
  or or_1 (or_1_out[0], A[0], B[0]);
  or or_2 (or_1_out[1], A[1], B[1]);
  or or_3 (or_1_out[2], A[2], B[2]);
  or or_4 (or_1_out[3], B[3], A[3]);
  and and_8 (and_8_out, and_1_out, OP[0]);
  comparador_cero comparador_cero_1 (.A(A), .Z(comparador_cero_1_z));
  inversor_4 inversor_4_1 (.A(B), .INV(OP[0]), .S(inversor_4_1_s));
  or or_5 (or_5_out, and_3_out, comparador_cero_1_z);
  not not_5 (not_5_out, and_8_out);
  xor xor_1 (xor_1_out, or_5_out, OP[0]);
  not not_6 (not_6_out, OP[0]);
  or or_6 (or_6_out, not_6_out, xor_1_out);
  sumador_flags sumador_flags_1 (
    .Cin(1'b0), .A(A), .B(inversor_4_1_s), .S(sumador_flags_1_s), .V(sumador_flags_1_v), .C(sumador_flags_1_c));  // open: N, Z
  and and_9 (and_9_out, or_6_out, multiplexer_3_out);
  not not_7 (not_7_out, sumador_flags_1_c);
  Multiplexer #(.width(4)) multiplexer_1 (.in0(and_4_out), .in1(or_1_out), .out(multiplexer_1_out), .sel(OP[0]));
  not not_8 (not_8_out, A[3]);
  Multiplexer multiplexer_2 (.in0(not_8_out), .in1(sumador_flags_1_v), .out(multiplexer_2_out), .sel(not_5_out));
  Multiplexer multiplexer_3 (.in0(sumador_flags_1_c), .in1(not_7_out), .out(multiplexer_3_out), .sel(OP[0]));
  Multiplexer #(.width(4)) multiplexer_4 (
    .in0(sumador_flags_1_s), .in1(multiplexer_1_out), .out({N, S[2:0]}), .sel(OP[1]));
  Hex_Digit_Display hex_digit_display_3 (.value({N, S[2:0]}));  // open: dp
  not not_9 (not_9_out, OP[1]);
  and and_10 (V, multiplexer_2_out, not_9_out);
  and and_11 (C, and_9_out, not_9_out);
  comparador_cero comparador_cero_2 (.A({N, S[2:0]}), .Z(Z));
  // Pins of 1 and 4 bits meet at B
  // Pins of 1 and 4 bits meet at A

  assign S[3] = N;
endmodule

module verificador (
  output [3:0] out_1,
  output [3:0] out_2,
  output [1:0] out_3,
  output halt,
  output N,
  output Z,
  output V,
  output C,
  output [3:0] res
);

  wire clock_1_out;

  Clock clock_1 (.out(clock_1_out));
  Counter #(.max('h3ff), .width(10)) counter_1 (
    .clk(clock_1_out), .carry(halt), .Q({out_3, out_2, out_1}));  // open: clr, load, up, count, D
  ALU alu_1 (.A(out_1), .B(out_2), .OP(out_3), .N(N), .Z(Z), .V(V), .C(C), .S(res));
endmodule
